# Fritzing sketch manual-gearbox-simulator (saved by Fritzing 0.9.3b)

parts:
  Part1 = Arduino Uno (Rev3)
  Part2 = Thumb Joystick
  OLED_I2C1 = OLED 128x64 I2C Monochrome Display

nets:
  N1: Part1.A0, Part2.HORZ
  N2: Part1.A1, Part2.VERT
  N3: Part1.A4/SDA, OLED_I2C1.SDA
  N4: Part1.A5/SCL, OLED_I2C1.SCK
  5V: Part1.5V, Part2.VCC, OLED_I2C1.VDD
  GND: Part1.GND, Part2.GND, Part2.SEL, OLED_I2C1.GND
